// Logisim project Logisim_Evolution.circ as structural Verilog: 5 circuits, main circuit bcd_to_binary
module main (
  input  in_1,
  input  in_2,
  input  in_3,
  input  in_4,
  input  in_5,
  input  in_6,
  input  in_7,
  input  in_8,
  input  in_9,
  input  in_10,
  input  in_11,
  input  in_12,
  input  [5:0] in_13,
  input  in_14,
  input  in_15,
  input  in_16,
  input  in_17,
  input  in_18,
  input  in_19,
  input  in_20,
  input  in_21,
  input  in_22,
  input  [1:0] in_23,
  input  [1:0] in_24,
  output [23:0] out_25,
  output [31:0] out_26,
  output [31:0] out_27,
  output [31:0] out_28,
  output [31:0] out_29,
  output [31:0] out_30,
  output [31:0] out_31,
  output [17:0] out_32,
  output [5:0] out_33,
  output out_34,
  output out_35,
  output out_36,
  output out_37,
  output out_38,
  output out_39,
  output out_40,
  output out_41,
  output [31:0] out_42,
  output out_43,
  output out_44,
  output out_45,
  output out_46,
  output out_47,
  output out_48,
  output out_49,
  output out_50
);

  wire and_2_out, and_3_out, and_4_out, and_5_out, and_6_out, and_8_out, and_9_out, and_10_out, and_11_out,
       and_12_out, and_13_out, and_14_out, and_18_out, and_24_out, and_28_out, and_29_out, and_30_out,
       and_31_out, and_34_out, and_35_out, and_37_out, and_40_out, and_41_out, and_42_out, and_43_out,
       and_44_out, and_45_out, and_46_out, and_47_out, and_48_out, and_52_out, and_53_out, and_54_out,
       and_55_out, and_59_out, and_60_out, and_65_out, and_66_out, and_68_out, and_85_out, and_86_out,
       and_87_out, and_88_out, and_89_out, and_90_out, and_91_out, and_92_out, and_111_out, and_112_out,
       and_113_out, and_114_out, and_115_out, and_116_out, button_1_out, clrregs, comparator_1_lt,
       comparator_3_eq, comparator_3_lt, comparator_4_eq, comparator_4_gt, comparator_5_lt, comparator_6_gt,
       comparator_7_eq, comparator_8_eq, d_ff_1_q, d_ff_2_q, d_ff_3_q, d_ff_4_q, d_ff_4_qn, d_ff_5_q,
       d_ff_5_qn, d_ff_15_q, d_ff_17_q, d_ff_18_q, d_ff_19_q, d_ff_21_q, d_ff_22_q, d_ff_23_q, d_ff_24_q,
       d_ff_25_q, d_ff_26_q, d_ff_28_q, d_ff_29_q, d_ff_30_q, d_ff_35_q, d_ff_36_q, d_ff_37_q, d_ff_38_q,
       d_ff_39_q, d_ff_40_q, d_ff_41_q, enable_print_9bcf9a48_out, glbclk, keyboard_1_avail,
       keyboard_2_avail, keyboard_3_avail, multiplexer_4_out, multiplexer_5_out, not_1_out, not_2_out,
       not_3_out, not_4_out, not_6_out, not_7_out, not_8_out, not_9_out, not_10_out, not_11_out, not_13_out,
       not_14_out, not_15_out, not_16_out, not_17_out, not_18_out, not_19_out, not_20_out, not_21_out,
       not_22_out, not_23_out, not_24_out, not_26_out, not_27_out, not_28_out, or_2_out, or_4_out, or_5_out,
       or_6_out, or_10_out, or_11_out, or_12_out, or_13_out, or_14_out, or_15_out, or_20_out, or_23_out,
       or_24_out, or_25_out, or_27_out, or_28_out, or_30_out, or_34_out, or_35_out, or_36_out, or_37_out,
       or_38_out, or_39_out, or_40_out, or_44_out, or_52_out, or_54_out, or_58_out, or_59_out, or_60_out,
       or_61_out, or_62_out, or_63_out, or_64_out, or_65_out, or_66_out, or_67_out, or_68_out, or_69_out,
       pc_clk, pc_count, pc_load, register_1_q, register_2_q, register_13_q, register_15_q, sp_hp_8f3679f7,
       undriven, update_sp_7b9e4477_out, update_stack_clock_before_d5e9d549_out,
       use_mem1_for_r2_40748cb5_out, write_data_at_addess_of_sp_to_reg_mem_1_77e2303b_out;
  wire [0:0] or_72_out;
  wire [1:0] or_17_out;
  wire [2:0] and_1_out, hp3;
  wire [6:0] d_ff_9_q, keyboard_2_data, keyboard_3_data;
  wire [7:0] and_61_out, and_62_out, and_63_out, and_64_out, or_42_out, ram_1_dout;
  wire [7:7] d_ff_31_q, d_ff_32_q, d_ff_33_q, d_ff_34_q;
  wire [13:0] counter_2_q, multiplexer_6_out, register_20_q;
  wire [14:0] ram_2_dout, register_20_q_2;
  wire [15:0] adder_1_out, adder_2_out, adder_4_out, adder_5_out, adder_6_out, and_7_out, and_16_out,
       and_17_out, and_19_out, and_23_out, and_25_out, and_26_out, and_27_out, and_32_out, and_36_out,
       and_38_out, and_39_out, and_57_out, and_58_out, and_67_out, and_84_out, dir_dec_be64acac_out,
       dir_wr_4fcbe2ae_out, mem_dec_r1_1cbb221e_out, mem_wr_r1_265633bc_out, multiplexer_1_out,
       multiplexer_2_out, multiplexer_3_out, or_8_out, or_9_out, or_18_out, or_19_out, or_22_out, or_33_out,
       or_43_out, or_57_out, pop_out, push_out, register_5_q, register_6_q, register_16_q, subtractor_1_out,
       subtractor_2_out, subtractor_3_out, subtractor_4_out, subtractor_5_out, subtractor_6_out,
       subtractor_7_out;
  wire [15:15] d_ff_6_q, d_ff_7_q, d_ff_8_q, d_ff_12_q, d_ff_12_qn, d_ff_27_q, d_ff_27_qn,
       dir_inc_e9448e49_out, mem_inc_r1_d00384f8_out, mem_write_ri_abd961e6_out, not_5_out, not_25_out,
       or_3_out, or_26_out, or_50_out, or_51_out, or_53_out, or_55_out, save_out,
       sub_r3_in_read_from_2_ed9042f6_out, sub_wr_out_wr_r2_d45307ea_out;
  wire [21:6] register_4_q;
  wire [23:0] and_20_out, and_21_out, and_22_out, ip, register_8_q, xnor_1_out;
  wire [23:23] and_15_out, reg1_jml_7c2a9e4f_out, reg2_jmo_5b1e7f97_out;
  wire [31:0] adder_3_out, adder_7_out, ALU_out, and_50_out, and_51_out, and_56_out, and_69_out, and_70_out,
       and_71_out, and_72_out, and_73_out, and_74_out, and_75_out, and_76_out, and_77_out, and_78_out,
       and_79_out, and_80_out, and_81_out, and_82_out, and_83_out, and_93_out, and_94_out, and_95_out,
       and_96_out, and_97_out, and_98_out, and_99_out, and_100_out, and_101_out, and_102_out, and_103_out,
       and_104_out, and_105_out, and_106_out, and_107_out, and_108_out, and_109_out, and_110_out,
       and_117_out, datareg1, demultiplexer_1_out0, demultiplexer_2_out0, divider_1_out, divider_2_out,
       L_r2_57be699c_out, led_matrix_module_1_out_0_53574313, led_matrix_module_1_out_1_2d638d36,
       led_matrix_module_1_out_3_89d83ed1, led_matrix_module_1_out_4_687d40bf, leyboard_out,
       multiplier_1_out, multiplier_2_out, negator_1_out, next_line_address_write_6f97db27_out, or_29_out,
       or_31_out, or_32_out, or_70_out, or_71_out, register_17_q, register_18_q, register_19_q,
       shifter_1_out, shifter_2_out, stack_write_d6dc388f_out, subtractor_8_out, subtractor_9_out, xnor_2_out;
  wire [31:22] register_3_q;
  wire [31:24] register_8_q_2;
  wire [31:29] register_20_q_3;
  wire [31:31] demultiplexer_2_out9, demultiplexer_3_out0, demultiplexer_3_out1, demultiplexer_3_out3,
       demultiplexer_3_out4, demultiplexer_3_out5, demultiplexer_3_out6, demultiplexer_3_out7,
       demultiplexer_3_out8, demultiplexer_3_out9, demultiplexer_3_out10, demultiplexer_3_out11,
       demultiplexer_3_out25, demultiplexer_3_out26, demultiplexer_3_out27, demultiplexer_3_out28,
       demultiplexer_3_out29, demultiplexer_3_out30, demultiplexer_3_out31, L_r2_as_write_a8c910e2_out,
       or_49_out;

  Counter #(.max('hffffff), .width(24)) counter_1 (
    .load(pc_load), .up(pc_count), .clk(pc_clk), .D(out_25), .Q(ip));  // open: clr, count, carry
  ROM #(.addrWidth(24), .dataWidth(32)) rom_1 (.addr(ip), .data(out_26));
  or or_1 (sp_hp_8f3679f7, and_1_out[2], and_1_out[1], and_1_out[0]);
  assign and_1_out = {hp3[0], hp3[1], hp3[2]} & {d_ff_8_q[15], d_ff_7_q[15], d_ff_6_q[15]};  // AND_Gate and_1, 3 bits wide
  assign xnor_1_out = ~(24'h24 ^ ip);  // XNOR_Gate xnor_1, 24 bits wide
  and and_2 (and_2_out, register_3_q[27], d_ff_6_q[15]);
  and and_3 (and_3_out, register_3_q[28], d_ff_7_q[15]);
  and and_4 (and_4_out, register_3_q[29], d_ff_8_q[15]);
  and and_5 (and_5_out, update_stack_clock_before_d5e9d549_out, d_ff_9_q[1]);
  or or_2 (or_2_out, in_21, and_6_out);
  and and_6 (and_6_out, xnor_1_out[23], xnor_1_out[22], xnor_1_out[21], xnor_1_out[20], xnor_1_out[19], xnor_1_out[18], xnor_1_out[17], xnor_1_out[16], xnor_1_out[15], xnor_1_out[14], xnor_1_out[13], xnor_1_out[12], xnor_1_out[11], xnor_1_out[10], xnor_1_out[9], xnor_1_out[8], xnor_1_out[7], xnor_1_out[6], xnor_1_out[5], xnor_1_out[4], xnor_1_out[3], xnor_1_out[2], xnor_1_out[1], xnor_1_out[0], in_22);
  assign and_7_out = {16{or_3_out[15]}} & or_57_out;  // AND_Gate and_7, 16 bits wide
  or or_3 (or_3_out[15], and_2_out, and_3_out, and_4_out);
  or or_4 (or_4_out, and_5_out, and_8_out);
  and and_8 (and_8_out, not_1_out, clrregs);
  not not_1 (not_1_out, update_stack_clock_before_d5e9d549_out);
  not not_2 (not_2_out, or_2_out);
  Register #(.width(1)) register_1 (.D(d_ff_9_q[3]), .clk(and_14_out), .Q(register_1_q));  // open: en, clr
  and and_9 (and_9_out, register_1_q, and_43_out);
  and and_10 (and_10_out, and_43_out, register_2_q);
  and and_11 (and_11_out, update_sp_7b9e4477_out, or_4_out);
  Register #(.width(1)) register_2 (.D(d_ff_9_q[1]), .clk(and_14_out), .Q(register_2_q));  // open: en, clr
  Register #(.width(32)) register_3 (
    .D({out_26[0], out_26[1], out_26[2], out_26[3], out_26[4], out_26[5], out_26[6], out_26[7], out_26[8], out_26[9], out_26[10], out_26[11], out_26[12], out_26[13], out_26[14], out_26[15], out_26[16], out_26[17], out_26[18], out_26[19], out_26[20], out_26[21], out_26[22], out_26[23], out_26[24], out_26[25], out_26[26], out_26[27], out_26[28], out_26[29], out_26[30], out_26[31]}),
    .clk(d_ff_3_q),
    .Q({register_3_q[31:27], hp3[0], hp3[1], hp3[2], register_3_q[23:22], out_27[0], out_27[1], out_27[2], out_27[3], out_27[4], out_27[5], out_27[6], out_27[7], out_27[8], out_27[9], out_27[10], out_27[11], out_27[12], out_27[13], out_27[14], out_27[15], out_27[16], out_27[17], out_27[18], out_27[19], out_27[20], out_27[21]}));  // open: en, clr
  Register #(.width(32)) register_4 (
    .D({out_26[0], out_26[1], out_26[2], out_26[3], out_26[4], out_26[5], out_26[6], out_26[7], out_26[8], out_26[9], out_26[10], out_26[11], out_26[12], out_26[13], out_26[14], out_26[15], out_26[16], out_26[17], out_26[18], out_26[19], out_26[20], out_26[21], out_26[22], out_26[23], out_26[24], out_26[25], out_26[26], out_26[27], out_26[28], out_26[29], out_26[30], out_26[31]}),
    .clk(d_ff_1_q),
    .Q({out_27[22], out_27[23], out_27[24], out_27[25], out_27[26], out_27[27], out_27[28], out_27[29], out_27[30], out_27[31], register_4_q, out_33[0], out_33[1], out_33[2], out_33[3], out_33[4], out_33[5]}));  // open: en, clr
  not not_3 (not_3_out, and_12_out);
  and and_12 (and_12_out, or_37_out, d_ff_4_q);
  and and_13 (and_13_out, not_2_out, or_14_out);
  or or_5 (or_5_out, d_ff_1_q, d_ff_9_q[0]);
  D_Flip_Flop d_ff_1 (.D(and_13_out), .clk(and_18_out), .Q(d_ff_1_q));  // open: Qn, preset, reset
  D_Flip_Flop d_ff_2 (.D(d_ff_1_q), .clk(and_18_out), .Q(d_ff_2_q));  // open: Qn, preset, reset
  D_Flip_Flop d_ff_3 (.D(d_ff_2_q), .clk(and_18_out), .Q(d_ff_3_q));  // open: Qn, preset, reset
  D_Flip_Flop d_ff_4 (.clk(or_5_out), .D(d_ff_4_qn), .Q(d_ff_4_q), .Qn(d_ff_4_qn));  // open: preset, reset
  and and_14 (and_14_out, not_4_out, and_18_out);
  Adder #(.width(16)) adder_1 (
    .a({{14{1'b0}}, register_3_q[30], register_3_q[31]}), .b(16'h1), .out(adder_1_out));  // open: cin, cout
  not not_4 (not_4_out, or_25_out);
  or or_6 (or_6_out, or_25_out, d_ff_1_q, d_ff_2_q, d_ff_3_q);
  and and_15 (and_15_out[23], not_8_out, not_9_out);
  assign out_25 = and_20_out | and_21_out | and_22_out;  // OR_Gate or_7, 24 bits wide
  Multiplexer #(.enable("true"), .width(16)) multiplexer_1 (
    .in0({register_4_q[6], register_4_q[7], register_4_q[8], register_4_q[9], register_4_q[10], register_4_q[11], register_4_q[12], register_4_q[13], register_4_q[14], register_4_q[15], register_4_q[16], register_4_q[17], register_4_q[18], register_4_q[19], register_4_q[20], register_4_q[21]}),
    .in1(register_5_q), .out(multiplexer_1_out), .sel(write_data_at_addess_of_sp_to_reg_mem_1_77e2303b_out));  // open: en
  assign or_8_out = and_16_out | and_17_out;  // OR_Gate or_8, 16 bits wide
  assign and_16_out = datareg1[15:0] & {16{not_5_out[15]}};  // AND_Gate and_16, 16 bits wide
  not not_5 (not_5_out[15], or_26_out[15]);
  Register #(.width(16)) register_5 (.D(or_9_out), .Q(register_5_q), .clk(and_11_out));  // open: en, clr
  assign or_9_out = mem_wr_r1_265633bc_out | dir_wr_4fcbe2ae_out | or_18_out | push_out | pop_out;  // OR_Gate or_9, 16 bits wide
  assign pop_out = adder_2_out & {16{or_51_out[15]}};  // AND_Gate pop, 16 bits wide
  Adder #(.width(16)) adder_2 (.a(register_5_q), .b(adder_1_out), .out(adder_2_out));  // open: cin, cout
  assign mem_wr_r1_265633bc_out = datareg1[15:0] & {16{mem_write_ri_abd961e6_out[15]}};  // AND_Gate mem_wr_r1_265633bc, 16 bits wide
  Clock clocksys (.out(glbclk));
  or or_10 (or_10_out, d_ff_8_q[15], d_ff_7_q[15], d_ff_6_q[15]);
  not not_6 (not_6_out, or_10_out);
  not not_7 (not_7_out, d_ff_5_q);
  D_Flip_Flop d_ff_5 (.D(d_ff_5_qn), .clk(and_40_out), .Q(d_ff_5_q), .Qn(d_ff_5_qn));  // open: preset, reset
  not not_8 (not_8_out, reg2_jmo_5b1e7f97_out[23]);
  not not_9 (not_9_out, reg1_jml_7c2a9e4f_out[23]);
  assign and_17_out = register_5_q & {16{or_26_out[15]}};  // AND_Gate and_17, 16 bits wide
  assign push_out = subtractor_1_out & {16{or_50_out[15]}};  // AND_Gate push, 16 bits wide
  Subtractor #(.width(16)) subtractor_1 (.a(register_5_q), .b(adder_1_out), .out(subtractor_1_out));  // open: bin, bout
  D_Flip_Flop d_ff_6 (.clk(or_12_out), .D(or_11_out), .Q(d_ff_6_q[15]));  // open: Qn, preset, reset
  or or_11 (or_11_out, not_6_out, d_ff_8_q[15]);
  or or_12 (or_12_out, d_ff_9_q[5], d_ff_9_q[3], d_ff_9_q[1]);
  or or_13 (or_13_out, or_6_out, d_ff_9_q[5], d_ff_9_q[4], d_ff_9_q[3], d_ff_9_q[2], d_ff_9_q[1], d_ff_9_q[0], d_ff_19_q);
  and and_18 (and_18_out, glbclk, not_7_out);
  Adder #(.width(32)) adder_3 (.a(datareg1), .b(32'h1), .out(adder_3_out));  // open: cin, cout
  Multiplexer #(.enable("true"), .width(16)) multiplexer_2 (
    .in0(out_27[31:16]), .in1(subtractor_2_out), .out(multiplexer_2_out), .sel(use_mem1_for_r2_40748cb5_out));  // open: en
  Subtractor #(.width(16)) subtractor_2 (
    .a(datareg1[15:0]), .b(and_19_out), .out(subtractor_2_out));  // open: bin, bout
  assign and_19_out = out_27[31:16] & {16{sub_r3_in_read_from_2_ed9042f6_out[15]}};  // AND_Gate and_19, 16 bits wide
  assign dir_wr_4fcbe2ae_out = out_27[15:0] & {16{save_out[15]}};  // AND_Gate dir_wr_4fcbe2ae, 16 bits wide
  D_Flip_Flop d_ff_7 (.clk(or_12_out), .D(d_ff_6_q[15]), .Q(d_ff_7_q[15]));  // open: Qn, preset, reset
  not not_10 (not_10_out, or_13_out);
  assign and_20_out = {24{reg2_jmo_5b1e7f97_out[23]}} & register_8_q;  // AND_Gate and_20, 24 bits wide
  assign and_21_out = {24{reg1_jml_7c2a9e4f_out[23]}} & adder_3_out[23:0];  // AND_Gate and_21, 24 bits wide
  assign and_22_out = {24{and_15_out[23]}} & out_27[23:0];  // AND_Gate and_22, 24 bits wide
  assign and_23_out = out_27[15:0] & {16{sub_wr_out_wr_r2_d45307ea_out[15]}};  // AND_Gate and_23, 16 bits wide
  assign dir_dec_be64acac_out = adder_5_out & {16{or_53_out[15]}};  // AND_Gate dir_dec_be64acac, 16 bits wide
  assign mem_dec_r1_1cbb221e_out = adder_4_out & {16{or_55_out[15]}};  // AND_Gate mem_dec_r1_1cbb221e, 16 bits wide
  Adder #(.width(16)) adder_4 (.a(register_5_q), .b(datareg1[15:0]), .out(adder_4_out));  // open: cin, cout
  D_Flip_Flop d_ff_8 (.clk(or_12_out), .D(d_ff_7_q[15]), .Q(d_ff_8_q[15]));  // open: Qn, preset, reset
  D_Flip_Flop d_ff_9 (.clk(and_18_out), .D(d_ff_3_q), .Q(d_ff_9_q[0]));  // open: Qn, preset, reset
  or or_14 (or_14_out, not_10_out, clrregs);
  or or_15 (or_15_out, and_24_out, and_34_out, out_32[9], and_35_out);
  and and_24 (and_24_out, and_54_out, out_32[7]);
  assign and_25_out = subtractor_3_out & {16{d_ff_8_q[15]}};  // AND_Gate and_25, 16 bits wide
  assign and_26_out = multiplexer_2_out & {16{d_ff_7_q[15]}};  // AND_Gate and_26, 16 bits wide
  assign and_27_out = multiplexer_1_out & {16{d_ff_6_q[15]}};  // AND_Gate and_27, 16 bits wide
  Multiplexer #(.enable("true"), .select(2), .width(16)) multiplexer_3 (
    .in0(out_27[15:0]), .in1(out_27[31:16]), .in2(multiplexer_1_out), .in3(or_8_out),
    .out(multiplexer_3_out), .sel(or_17_out));  // open: en
  or or_16 (or_17_out[1], and_28_out, and_30_out);
  or or_17 (or_17_out[0], and_29_out, and_31_out);
  and and_28 (and_28_out, not_11_out, not_14_out, out_32[15]);
  and and_29 (and_29_out, out_32[16], not_14_out, out_32[15]);
  and and_30 (and_30_out, not_11_out, not_13_out, or_60_out);
  and and_31 (and_31_out, not_11_out, not_13_out, or_60_out);
  assign or_18_out = dir_dec_be64acac_out | mem_dec_r1_1cbb221e_out | and_32_out | and_36_out;  // OR_Gate or_18, 16 bits wide
  Adder #(.width(16)) adder_5 (.a(register_5_q), .b(out_27[15:0]), .out(adder_5_out));  // open: cin, cout
  assign and_32_out = subtractor_5_out & {16{mem_inc_r1_d00384f8_out[15]}};  // AND_Gate and_32, 16 bits wide
  D_Flip_Flop d_ff_10 (.clk(and_18_out), .D(d_ff_9_q[0]), .Q(d_ff_9_q[1]));  // open: Qn, preset, reset
  and and_33 (pc_load, not_3_out, or_15_out);
  and and_34 (and_34_out, and_53_out, out_32[6]);
  and and_35 (and_35_out, d_ff_26_q, out_32[5]);
  assign or_19_out = and_25_out | and_26_out | and_27_out;  // OR_Gate or_19, 16 bits wide
  Subtractor #(.width(16)) subtractor_3 (
    .a(multiplexer_3_out), .b(and_23_out), .out(subtractor_3_out));  // open: bin, bout
  not not_11 (not_11_out, out_32[16]);
  assign and_36_out = subtractor_4_out & {16{dir_inc_e9448e49_out[15]}};  // AND_Gate and_36, 16 bits wide
  Subtractor #(.width(16)) subtractor_4 (
    .a(register_5_q), .b(out_27[15:0]), .out(subtractor_4_out));  // open: bin, bout
  Subtractor #(.width(16)) subtractor_5 (
    .a(register_5_q), .b(datareg1[15:0]), .out(subtractor_5_out));  // open: bin, bout
  and and_37 (and_37_out, xnor_2_out[0], xnor_2_out[1], xnor_2_out[2], xnor_2_out[3], xnor_2_out[4], xnor_2_out[5], xnor_2_out[6], xnor_2_out[7], xnor_2_out[8], xnor_2_out[9], xnor_2_out[10], xnor_2_out[11], xnor_2_out[12], xnor_2_out[13], xnor_2_out[14], xnor_2_out[15], xnor_2_out[17], xnor_2_out[18], xnor_2_out[19], xnor_2_out[20], xnor_2_out[21], xnor_2_out[22], xnor_2_out[23], xnor_2_out[24], xnor_2_out[25], xnor_2_out[26], xnor_2_out[27], xnor_2_out[28], xnor_2_out[29], xnor_2_out[30], xnor_2_out[31], xnor_2_out[16]);
  D_Flip_Flop d_ff_11 (.clk(and_18_out), .D(and_10_out), .Q(d_ff_9_q[2]));  // open: Qn, preset, reset
  or or_20 (or_20_out, d_ff_9_q[2], d_ff_9_q[4]);
  D_Flip_Flop d_ff_12 (
    .clk(d_ff_15_q), .D(1'b1), .Q(d_ff_12_q[15]), .Qn(d_ff_12_qn[15]), .reset(or_20_out));  // open: preset
  assign and_38_out = adder_6_out & {16{d_ff_12_qn[15]}};  // AND_Gate and_38, 16 bits wide
  not not_12 (pc_count, pc_load);
  or or_21 (pc_clk, d_ff_2_q, clrregs);
  Adder #(.width(16)) adder_6 (.a(and_7_out), .b(or_19_out), .out(adder_6_out));  // open: cin, cout
  not not_13 (not_13_out, out_32[15]);
  not not_14 (not_14_out, or_60_out);
  D_Flip_Flop d_ff_13 (.clk(and_18_out), .D(d_ff_9_q[2]), .Q(d_ff_9_q[3]));  // open: Qn, preset, reset
  assign and_39_out = {16{d_ff_12_q[15]}} & subtractor_6_out;  // AND_Gate and_39, 16 bits wide
  assign or_22_out = and_38_out | and_39_out;  // OR_Gate or_22, 16 bits wide
  or or_23 (or_23_out, d_ff_9_q[1], d_ff_9_q[3], and_42_out);
  or or_24 (or_24_out, d_ff_15_q, d_ff_17_q, d_ff_18_q);
  or or_25 (or_25_out, or_24_out, or_35_out);
  D_Flip_Flop d_ff_14 (.clk(and_18_out), .D(and_9_out), .Q(d_ff_9_q[4]));  // open: Qn, preset, reset
  and and_40 (and_40_out, d_ff_9_q[5], out_32[12], not_15_out);
  Subtractor #(.width(16)) subtractor_6 (.a(register_6_q), .b(16'h1), .out(subtractor_6_out));  // open: bin, bout
  Register #(.width(16)) register_6 (.D(or_22_out), .Q(register_6_q), .clk(d_ff_15_q), .clr(or_20_out));  // open: en
  D_Flip_Flop d_ff_15 (.clk(and_18_out), .D(or_23_out), .Q(d_ff_15_q), .reset(or_20_out));  // open: Qn, preset
  D_Flip_Flop d_ff_16 (.clk(and_18_out), .D(d_ff_9_q[4]), .Q(d_ff_9_q[5]));  // open: Qn, preset, reset
  not not_15 (not_15_out, and_90_out);
  D_Flip_Flop d_ff_17 (.clk(and_18_out), .D(d_ff_15_q), .Q(d_ff_17_q), .reset(or_20_out));  // open: Qn, preset
  and and_41 (and_41_out, d_ff_19_q, out_32[17]);
  D_Flip_Flop d_ff_18 (.clk(and_18_out), .D(d_ff_17_q), .Q(d_ff_18_q), .reset(or_20_out));  // open: Qn, preset
  not not_16 (not_16_out, multiplexer_4_out);
  and and_42 (and_42_out, d_ff_18_q, not_16_out);
  not not_17 (not_17_out, out_33[5]);
  Demultiplexer #(.enable("true"), .select(5)) demultiplexer_1 (
    .out0(demultiplexer_1_out0[0]), .out1(demultiplexer_1_out0[1]), .out2(demultiplexer_1_out0[2]),
    .out3(demultiplexer_1_out0[3]), .out4(demultiplexer_1_out0[4]), .out5(demultiplexer_1_out0[5]),
    .out6(demultiplexer_1_out0[6]), .out7(demultiplexer_1_out0[7]), .out8(demultiplexer_1_out0[8]),
    .out9(demultiplexer_1_out0[9]), .out10(demultiplexer_1_out0[10]), .out11(demultiplexer_1_out0[11]),
    .out12(demultiplexer_1_out0[12]), .out13(demultiplexer_1_out0[13]), .out14(demultiplexer_1_out0[14]),
    .out15(demultiplexer_1_out0[15]), .out16(demultiplexer_1_out0[16]), .out17(demultiplexer_1_out0[17]),
    .out18(demultiplexer_1_out0[18]), .out19(demultiplexer_1_out0[19]), .out20(demultiplexer_1_out0[20]),
    .out21(demultiplexer_1_out0[21]), .out22(demultiplexer_1_out0[22]), .out23(demultiplexer_1_out0[23]),
    .out24(demultiplexer_1_out0[24]), .out25(demultiplexer_1_out0[25]), .out26(demultiplexer_1_out0[26]),
    .out27(demultiplexer_1_out0[27]), .out28(demultiplexer_1_out0[28]), .out29(demultiplexer_1_out0[29]),
    .out30(demultiplexer_1_out0[30]), .out31(demultiplexer_1_out0[31]), .in(not_17_out), .sel(out_33[4:0]));  // open: en
  Demultiplexer #(.enable("true"), .select(5)) demultiplexer_2 (
    .out0(demultiplexer_2_out0[0]), .out1(demultiplexer_2_out0[1]), .out2(demultiplexer_2_out0[2]),
    .out3(demultiplexer_2_out0[3]), .out4(demultiplexer_2_out0[4]), .out5(demultiplexer_2_out0[5]),
    .out6(demultiplexer_2_out0[6]), .out7(demultiplexer_2_out0[7]), .out8(demultiplexer_2_out0[8]),
    .out9(demultiplexer_2_out9[31]), .out10(demultiplexer_2_out0[10]), .out11(demultiplexer_2_out0[11]),
    .out12(demultiplexer_2_out0[12]), .out13(demultiplexer_2_out0[13]), .out14(demultiplexer_2_out0[14]),
    .out15(demultiplexer_2_out0[15]), .out16(demultiplexer_2_out0[16]), .out17(demultiplexer_2_out0[17]),
    .out18(demultiplexer_2_out0[18]), .out19(demultiplexer_2_out0[19]), .out20(demultiplexer_2_out0[20]),
    .out21(demultiplexer_2_out0[21]), .out22(demultiplexer_2_out0[22]), .out23(demultiplexer_2_out0[23]),
    .out24(demultiplexer_2_out0[24]), .out25(demultiplexer_2_out0[25]), .out26(demultiplexer_2_out0[26]),
    .out27(demultiplexer_2_out0[27]), .out28(demultiplexer_2_out0[28]), .out29(demultiplexer_2_out0[29]),
    .out30(demultiplexer_2_out0[30]), .out31(demultiplexer_2_out0[31]), .in(out_33[5]), .sel(out_33[4:0]));  // open: en
  D_Flip_Flop d_ff_19 (.clk(and_18_out), .D(d_ff_9_q[5]), .Q(d_ff_19_q));  // open: Qn, preset, reset
  D_Flip_Flop d_ff_20 (.clk(and_18_out), .D(d_ff_9_q[6]), .Q(clrregs));  // open: Qn, preset, reset
  and and_43 (and_43_out, d_ff_18_q, multiplexer_4_out);
  or or_26 (or_26_out[15], demultiplexer_2_out0[10], demultiplexer_2_out0[0], demultiplexer_2_out0[2], demultiplexer_1_out0[31]);
  or or_27 (or_27_out, not_18_out, d_ff_24_q);
  or or_28 (or_28_out, demultiplexer_1_out0[22], demultiplexer_2_out0[23], demultiplexer_2_out0[24], demultiplexer_2_out0[25], demultiplexer_1_out0[23], demultiplexer_2_out0[30]);
  or use_mem1_for_r2_40748cb5 (use_mem1_for_r2_40748cb5_out, demultiplexer_2_out0[14], demultiplexer_2_out0[15], demultiplexer_2_out0[19], demultiplexer_2_out0[16]);
  or update_stack_clock_before_d5e9d549 (update_stack_clock_before_d5e9d549_out, demultiplexer_2_out0[16], demultiplexer_2_out0[17], demultiplexer_2_out0[1]);
  Register #(.width(32)) register_7 (.D(out_31), .Q(datareg1), .clk(d_ff_9_q[2]));  // open: en, clr
  Register #(.width(32)) register_8 (
    .D(out_31), .Q({register_8_q_2, register_8_q}), .clk(d_ff_9_q[4]));  // open: en, clr
  D_Flip_Flop d_ff_21 (.clk(d_ff_17_q), .D(or_27_out), .Q(d_ff_21_q), .reset(or_20_out));  // open: Qn, preset
  D_Flip_Flop d_ff_22 (.clk(d_ff_17_q), .D(d_ff_21_q), .Q(d_ff_22_q), .reset(or_20_out));  // open: Qn, preset
  D_Flip_Flop d_ff_23 (.clk(d_ff_17_q), .D(d_ff_22_q), .Q(d_ff_23_q), .reset(or_20_out));  // open: Qn, preset
  D_Flip_Flop d_ff_24 (.clk(d_ff_17_q), .D(d_ff_23_q), .Q(d_ff_24_q), .reset(or_20_out));  // open: Qn, preset
  assign or_29_out = leyboard_out | and_56_out | or_32_out | L_r2_57be699c_out | ALU_out;  // OR_Gate or_29, 32 bits wide
  or sub_wr_out_wr_r2_d45307ea (sub_wr_out_wr_r2_d45307ea_out[15], demultiplexer_2_out0[15], demultiplexer_2_out0[18], demultiplexer_2_out0[13]);
  Register register_9 (.D(ram_1_dout), .Q(out_31[7:0]), .clk(and_44_out), .clr(clrregs));  // open: en
  and and_44 (and_44_out, d_ff_21_q, d_ff_18_q);
  Register register_10 (.D(ram_1_dout), .Q(out_31[15:8]), .clk(and_45_out), .clr(clrregs));  // open: en
  and and_45 (and_45_out, d_ff_22_q, d_ff_18_q);
  Register register_11 (.D(ram_1_dout), .Q(out_31[23:16]), .clk(and_46_out), .clr(clrregs));  // open: en
  and and_46 (and_46_out, d_ff_23_q, d_ff_18_q);
  Register register_12 (.D(ram_1_dout), .Q(out_31[31:24]), .clk(and_47_out), .clr(clrregs));  // open: en
  and and_47 (and_47_out, d_ff_24_q, d_ff_18_q);
  assign leyboard_out = {{25{1'b0}}, out_29[6:0]} & {32{out_32[13]}};  // AND_Gate leyboard, 32 bits wide
  assign ALU_out = {32{out_32[14]}} & out_42;  // AND_Gate ALU, 32 bits wide
  assign L_r2_57be699c_out = {32{L_r2_as_write_a8c910e2_out[31]}} & {register_8_q_2, register_8_q};  // AND_Gate L_r2_57be699c, 32 bits wide
  or write_en_5c11cffd (out_32[17], or_28_out, demultiplexer_1_out0[1], demultiplexer_1_out0[2], demultiplexer_1_out0[3], demultiplexer_1_out0[4], demultiplexer_1_out0[5], demultiplexer_1_out0[6], demultiplexer_1_out0[7], demultiplexer_1_out0[8], demultiplexer_1_out0[9], demultiplexer_1_out0[10], demultiplexer_1_out0[11], demultiplexer_1_out0[17], demultiplexer_1_out0[18], demultiplexer_1_out0[23], demultiplexer_1_out0[30], demultiplexer_1_out0[31], demultiplexer_2_out0[0], demultiplexer_2_out0[2], demultiplexer_2_out9[31], demultiplexer_2_out0[10], demultiplexer_2_out0[13], demultiplexer_2_out0[14], demultiplexer_2_out0[15], demultiplexer_2_out0[18], demultiplexer_2_out0[19], demultiplexer_2_out0[1], demultiplexer_2_out0[22], demultiplexer_2_out0[26], demultiplexer_2_out0[27], demultiplexer_2_out0[28], demultiplexer_2_out0[29]);
  buf reg1_jml_7c2a9e4f (reg1_jml_7c2a9e4f_out[23], demultiplexer_2_out0[17]);  // OR_Gate
  or or_30 (or_30_out, d_ff_22_q, d_ff_23_q, d_ff_24_q, d_ff_21_q);
  not not_18 (not_18_out, or_30_out);
  Multiplexer #(.enable("true"), .select(2)) multiplexer_4 (
    .in0(d_ff_21_q), .in1(d_ff_22_q), .in2(d_ff_23_q), .in3(d_ff_24_q), .out(multiplexer_4_out),
    .sel({register_3_q[30], register_3_q[31]}));  // open: en
  buf reg2_jmo_5b1e7f97 (reg2_jmo_5b1e7f97_out[23], demultiplexer_2_out0[16]);  // OR_Gate
  // OR_Gate update_comp_reg_ad1d29f2: pin names not known; wires that end beside it: demultiplexer_1_out0[12], demultiplexer_1_out0[13], out_32[8], out_43, in_14
  assign xnor_2_out = ~(datareg1 ^ or_31_out);  // XNOR_Gate xnor_2, 32 bits wide
  and and_48 (and_48_out, d_ff_19_q, out_32[8]);
  or write_data_at_addess_of_sp_to_reg_mem_1_77e2303b (write_data_at_addess_of_sp_to_reg_mem_1_77e2303b_out, demultiplexer_2_out0[16], demultiplexer_2_out0[17], demultiplexer_2_out0[1]);
  D_Flip_Flop d_ff_25 (.clk(and_48_out), .D(comparator_1_lt), .Q(d_ff_25_q));  // open: Qn, preset, reset
  D_Flip_Flop d_ff_26 (.clk(and_48_out), .D(and_37_out), .Q(d_ff_26_q));  // open: Qn, preset, reset
  // Telnet telnet_1: pin names not known
  and and_49 (d_ff_9_q[6], register_13_q, and_60_out);
  Register #(.width(1)) register_13 (.D(d_ff_19_q), .Q(register_13_q), .clk(and_55_out));  // open: en, clr
  Register #(.width(32)) register_14 (.D({{25{1'b0}}, out_30[6:0]}), .Q(out_28), .clk(and_90_out));  // open: en, clr
  Comparator #(.width(32)) comparator_1 (.a(datareg1), .b(or_31_out), .lt(comparator_1_lt));  // open: gt, eq
  not not_19 (not_19_out, d_ff_25_q);
  not not_20 (not_20_out, d_ff_26_q);
  assign and_50_out = {register_8_q_2, register_8_q} & {32{out_32[11]}};  // AND_Gate and_50, 32 bits wide
  assign and_51_out = {32{out_32[10]}} & out_27;  // AND_Gate and_51, 32 bits wide
  and and_52 (and_52_out, and_60_out, register_15_q);
  or write_3_7f7e4ff9 (out_32[16], demultiplexer_1_out0[1], demultiplexer_1_out0[2], demultiplexer_1_out0[3], demultiplexer_1_out0[4], demultiplexer_1_out0[5], demultiplexer_2_out0[14], demultiplexer_2_out0[15], demultiplexer_2_out0[19], demultiplexer_2_out0[1], demultiplexer_2_out0[22], demultiplexer_2_out0[23], demultiplexer_2_out0[24], demultiplexer_2_out0[25], demultiplexer_2_out0[26], demultiplexer_2_out0[27], demultiplexer_2_out0[28], demultiplexer_2_out0[29], demultiplexer_2_out0[30], demultiplexer_1_out0[22], demultiplexer_1_out0[23]);
  // OR_Gate if_grter_a6aa8c5e: pin names not known; wires that end beside it: in_14, demultiplexer_1_out0[14], out_32[7], out_44, in_15
  and and_53 (and_53_out, d_ff_25_q, not_20_out);
  and and_54 (and_54_out, not_20_out, not_19_out);
  assign or_31_out = and_50_out | and_51_out;  // OR_Gate or_31, 32 bits wide
  Comparator #(.width(2)) comparator_2 (.a(in_23), .b(in_24), .lt(out_50));  // open: gt, eq
  and and_55 (and_55_out, not_21_out, and_18_out);
  Register #(.width(1)) register_15 (.D(in_4), .Q(register_15_q), .clk(and_55_out));  // open: en, clr
  assign and_56_out = out_28 & {32{out_32[12]}};  // AND_Gate and_56, 32 bits wide
  not not_21 (not_21_out, or_35_out);
  assign or_32_out = next_line_address_write_6f97db27_out | stack_write_d6dc388f_out;  // OR_Gate or_32, 32 bits wide
  buf sub_r3_in_read_from_2_ed9042f6 (sub_r3_in_read_from_2_ed9042f6_out[15], demultiplexer_2_out0[19]);  // OR_Gate
  assign next_line_address_write_6f97db27_out = {{8{1'b0}}, ip} & {32{or_49_out[31]}};  // AND_Gate next_line_address_write_6f97db27, 32 bits wide
  D_Flip_Flop d_ff_27 (
    .clk(d_ff_28_q), .D(1'b1), .Q(d_ff_27_q[15]), .Qn(d_ff_27_qn[15]), .reset(clrregs));  // open: preset
  assign and_57_out = adder_6_out & {16{d_ff_27_qn[15]}};  // AND_Gate and_57, 16 bits wide
  assign and_58_out = {16{d_ff_27_q[15]}} & subtractor_7_out;  // AND_Gate and_58, 16 bits wide
  assign or_33_out = and_57_out | and_58_out;  // OR_Gate or_33, 16 bits wide
  or write_1_faa557a3 (out_32[15], demultiplexer_1_out0[6], demultiplexer_1_out0[7], demultiplexer_1_out0[8], demultiplexer_1_out0[9], demultiplexer_1_out0[10], demultiplexer_1_out0[11], demultiplexer_1_out0[17], demultiplexer_1_out0[18], demultiplexer_2_out9[31], demultiplexer_2_out0[13]);
  // OR_Gate if_less_e35d2328: pin names not known; wires that end beside it: in_15, demultiplexer_1_out0[15], out_32[6], out_45, in_16
  Subtractor #(.width(16)) subtractor_7 (.a(register_16_q), .b(16'h1), .out(subtractor_7_out));  // open: bin, bout
  Register #(.width(16)) register_16 (.D(or_33_out), .Q(register_16_q), .clk(d_ff_28_q), .clr(clrregs));  // open: en
  D_Flip_Flop d_ff_28 (.clk(and_18_out), .D(or_34_out), .Q(d_ff_28_q), .reset(clrregs));  // open: Qn, preset
  or or_34 (or_34_out, in_4, d_ff_19_q, and_59_out);
  or or_35 (or_35_out, d_ff_28_q, d_ff_29_q, d_ff_30_q);
  D_Flip_Flop d_ff_29 (.clk(and_18_out), .D(d_ff_28_q), .Q(d_ff_29_q), .reset(clrregs));  // open: Qn, preset
  or or_36 (or_36_out, demultiplexer_2_out0[30], demultiplexer_2_out0[29], demultiplexer_1_out0[1]);
  or or_37 (or_37_out, out_32[7], out_32[6], out_32[5], out_32[9]);
  D_Flip_Flop d_ff_30 (.clk(and_18_out), .D(d_ff_29_q), .Q(d_ff_30_q), .reset(clrregs));  // open: Qn, preset
  not not_22 (not_22_out, multiplexer_5_out);
  and and_59 (and_59_out, d_ff_30_q, not_22_out);
  and and_60 (and_60_out, d_ff_30_q, multiplexer_5_out);
  assign stack_write_d6dc388f_out = {{16{1'b0}}, register_5_q} & {32{demultiplexer_2_out9[31]}};  // AND_Gate stack_write_d6dc388f, 32 bits wide
  or alu_write_5a81f5e1 (out_32[14], or_36_out, or_39_out, demultiplexer_1_out0[2], demultiplexer_1_out0[3], demultiplexer_1_out0[4], demultiplexer_1_out0[5], demultiplexer_1_out0[6], demultiplexer_1_out0[7], demultiplexer_1_out0[8], demultiplexer_1_out0[9], demultiplexer_1_out0[10], demultiplexer_1_out0[11], demultiplexer_1_out0[12], demultiplexer_1_out0[13], demultiplexer_1_out0[19], demultiplexer_1_out0[20], demultiplexer_1_out0[22], demultiplexer_1_out0[23], demultiplexer_1_out0[24], demultiplexer_1_out0[25], demultiplexer_1_out0[28], demultiplexer_1_out0[29], demultiplexer_2_out0[0], demultiplexer_2_out0[2], demultiplexer_2_out0[1], demultiplexer_2_out0[22], demultiplexer_2_out0[23], demultiplexer_2_out0[24], demultiplexer_2_out0[25], demultiplexer_2_out0[26], demultiplexer_2_out0[27], demultiplexer_2_out0[28]);
  or or_38 (or_38_out, not_23_out, d_ff_34_q[7]);
  // OR_Gate if_eql_709c241f: pin names not known; wires that end beside it: in_16, demultiplexer_1_out0[16], out_32[5], out_46, in_17
  D_Flip_Flop d_ff_31 (.clk(d_ff_29_q), .D(or_38_out), .Q(d_ff_31_q[7]), .reset(clrregs));  // open: Qn, preset
  D_Flip_Flop d_ff_32 (.clk(d_ff_29_q), .D(d_ff_31_q[7]), .Q(d_ff_32_q[7]), .reset(clrregs));  // open: Qn, preset
  D_Flip_Flop d_ff_33 (.clk(d_ff_29_q), .D(d_ff_32_q[7]), .Q(d_ff_33_q[7]), .reset(clrregs));  // open: Qn, preset
  D_Flip_Flop d_ff_34 (.clk(d_ff_29_q), .D(d_ff_33_q[7]), .Q(d_ff_34_q[7]), .reset(clrregs));  // open: Qn, preset
  or or_39 (or_39_out, demultiplexer_1_out0[22], demultiplexer_1_out0[23]);
  or or_40 (or_40_out, d_ff_32_q[7], d_ff_33_q[7], d_ff_34_q[7], d_ff_31_q[7]);
  Multiplexer #(.enable("true"), .select(2)) multiplexer_5 (
    .in0(d_ff_31_q[7]), .in1(d_ff_32_q[7]), .in2(d_ff_33_q[7]), .in3(d_ff_34_q[7]), .out(multiplexer_5_out),
    .sel({register_3_q[30], register_3_q[31]}));  // open: en
  assign and_61_out = or_29_out[7:0] & {8{d_ff_31_q[7]}};  // AND_Gate and_61, 8 bits wide
  assign and_62_out = or_29_out[15:8] & {8{d_ff_32_q[7]}};  // AND_Gate and_62, 8 bits wide
  assign and_63_out = or_29_out[23:16] & {8{d_ff_33_q[7]}};  // AND_Gate and_63, 8 bits wide
  assign and_64_out = or_29_out[31:24] & {8{d_ff_34_q[7]}};  // AND_Gate and_64, 8 bits wide
  not not_23 (not_23_out, or_40_out);
  buf event_listener_b865028d (out_32[13], demultiplexer_1_out0[17]);  // OR_Gate
  or or_41 (out_32[4], demultiplexer_1_out0[1], demultiplexer_1_out0[2], demultiplexer_1_out0[3], demultiplexer_1_out0[6], demultiplexer_1_out0[7], demultiplexer_1_out0[8], demultiplexer_1_out0[9], demultiplexer_1_out0[12], demultiplexer_1_out0[13], demultiplexer_1_out0[4], demultiplexer_1_out0[20], demultiplexer_1_out0[22], demultiplexer_1_out0[23], demultiplexer_1_out0[25], demultiplexer_1_out0[29], demultiplexer_2_out0[2]);
  assign or_42_out = and_61_out | and_62_out | and_63_out | and_64_out;  // OR_Gate or_42, 8 bits wide
  Button button_1 (.out(button_1_out));
  assign or_43_out = register_16_q | register_6_q;  // OR_Gate or_43, 16 bits wide
  RAM #(.addrWidth(16), .enables("line")) ram_1 (
    .addr(or_43_out), .we(out_32[17]), .clk(or_44_out), .din(or_42_out), .dout(ram_1_dout));
  or or_44 (or_44_out, button_1_out, and_65_out);
  and and_65 (and_65_out, d_ff_30_q, out_32[17]);
  buf user_input_74e1e213 (out_32[12], demultiplexer_1_out0[18]);  // OR_Gate
  or or_45 (out_32[3], demultiplexer_1_out0[1], demultiplexer_1_out0[2], demultiplexer_1_out0[3], demultiplexer_1_out0[6], demultiplexer_1_out0[7], demultiplexer_1_out0[8], demultiplexer_1_out0[9], demultiplexer_1_out0[12], demultiplexer_1_out0[13], demultiplexer_1_out0[4], demultiplexer_1_out0[20], demultiplexer_1_out0[22], demultiplexer_1_out0[23], demultiplexer_1_out0[25], demultiplexer_1_out0[29], demultiplexer_2_out0[2], demultiplexer_2_out0[27], demultiplexer_2_out0[28], demultiplexer_2_out0[29], demultiplexer_2_out0[30]);
  TTY #(.cols(120), .rows(40)) tty_1 (.data(or_29_out[6:0]), .clk(d_ff_19_q), .we(or_61_out), .clr(and_87_out));
  or reg_read_0c0782a0 (out_32[11], demultiplexer_1_out0[1], demultiplexer_1_out0[2], demultiplexer_1_out0[3], demultiplexer_1_out0[4], demultiplexer_1_out0[5], demultiplexer_1_out0[12], demultiplexer_2_out0[22], demultiplexer_2_out0[23], demultiplexer_2_out0[24], demultiplexer_2_out0[25], demultiplexer_2_out0[26], demultiplexer_2_out0[27], demultiplexer_2_out0[28], demultiplexer_2_out0[29], demultiplexer_2_out0[30], demultiplexer_1_out0[22], demultiplexer_1_out0[23]);
  or or_46 (out_32[2], demultiplexer_1_out0[1], demultiplexer_1_out0[2], demultiplexer_1_out0[3], demultiplexer_1_out0[6], demultiplexer_1_out0[7], demultiplexer_1_out0[8], demultiplexer_1_out0[9], demultiplexer_1_out0[12], demultiplexer_1_out0[13], demultiplexer_1_out0[4], demultiplexer_1_out0[20], demultiplexer_1_out0[25], demultiplexer_1_out0[29], demultiplexer_2_out0[2], demultiplexer_2_out0[23], demultiplexer_2_out0[24], demultiplexer_2_out0[25], demultiplexer_2_out0[26]);
  or direct_read_bc8b1012 (out_32[10], demultiplexer_1_out0[6], demultiplexer_1_out0[7], demultiplexer_1_out0[8], demultiplexer_1_out0[9], demultiplexer_1_out0[10], demultiplexer_1_out0[11], demultiplexer_1_out0[13], demultiplexer_1_out0[19], demultiplexer_1_out0[20], demultiplexer_1_out0[24], demultiplexer_1_out0[25], demultiplexer_1_out0[28], demultiplexer_1_out0[29], demultiplexer_2_out0[0], demultiplexer_2_out0[2], demultiplexer_2_out0[1]);
  or or_47 (out_32[1], demultiplexer_1_out0[1], demultiplexer_1_out0[2], demultiplexer_1_out0[6], demultiplexer_1_out0[7], demultiplexer_1_out0[12], demultiplexer_1_out0[13], demultiplexer_1_out0[20], demultiplexer_1_out0[22], demultiplexer_1_out0[23], demultiplexer_1_out0[25], demultiplexer_1_out0[29], demultiplexer_2_out0[2], demultiplexer_2_out0[22], demultiplexer_2_out0[25], demultiplexer_2_out0[26], demultiplexer_2_out0[29], demultiplexer_2_out0[30]);
  or jmp (out_32[9], demultiplexer_1_out0[26], demultiplexer_2_out0[10], demultiplexer_2_out0[16], demultiplexer_2_out0[17]);
  Keyboard keyboard_1 (.clk(and_91_out), .avail(keyboard_1_avail), .data(out_30[6:0]));  // open: re, clr
  or or_48 (out_32[0], demultiplexer_1_out0[1], demultiplexer_1_out0[3], demultiplexer_1_out0[5], demultiplexer_1_out0[6], demultiplexer_1_out0[8], demultiplexer_1_out0[10], demultiplexer_1_out0[20], demultiplexer_1_out0[22], demultiplexer_1_out0[25], demultiplexer_1_out0[29], demultiplexer_2_out0[2], demultiplexer_2_out0[4], demultiplexer_2_out0[1], demultiplexer_2_out0[22], demultiplexer_2_out0[24], demultiplexer_2_out0[26], demultiplexer_2_out0[28], demultiplexer_2_out0[30]);
  RAM #(.addrWidth(14), .dataWidth(15), .readbehav("war")) ram_2 (
    .addr(multiplexer_6_out), .we(in_1), .clk(glbclk), .din(register_20_q_2), .dout(ram_2_dout));  // open: oe
  Multiplexer #(.width(14)) multiplexer_6 (.in0(counter_2_q), .in1(register_20_q), .out(multiplexer_6_out), .sel(in_3));
  or or_49 (or_49_out[31], demultiplexer_1_out0[31], demultiplexer_2_out0[10]);
  or L_r2_as_write_a8c910e2 (L_r2_as_write_a8c910e2_out[31], demultiplexer_2_out0[19], demultiplexer_1_out0[30], demultiplexer_2_out0[13], demultiplexer_2_out0[14], demultiplexer_2_out0[15], demultiplexer_2_out0[18]);
  or or_50 (or_50_out[15], demultiplexer_1_out0[31], demultiplexer_2_out0[0], demultiplexer_2_out0[2], demultiplexer_2_out0[10]);
  or or_51 (or_51_out[15], demultiplexer_2_out0[1], demultiplexer_2_out0[17], demultiplexer_2_out0[16]);
  buf save (save_out[15], demultiplexer_2_out0[3]);  // OR_Gate
  or update_sp_7b9e4477 (update_sp_7b9e4477_out, demultiplexer_2_out0[2], demultiplexer_2_out0[6], demultiplexer_2_out0[5], demultiplexer_2_out0[0], demultiplexer_2_out0[8], demultiplexer_2_out0[1], demultiplexer_2_out0[3], demultiplexer_2_out0[4], or_52_out);
  or or_52 (or_52_out, demultiplexer_2_out0[7], demultiplexer_2_out0[16], demultiplexer_2_out0[10], demultiplexer_1_out0[31], or_54_out);
  buf or_53 (or_53_out[15], demultiplexer_2_out0[7]);  // OR_Gate
  buf dir_inc_e9448e49 (dir_inc_e9448e49_out[15], demultiplexer_2_out0[5]);  // OR_Gate
  buf mem_write_ri_abd961e6 (mem_write_ri_abd961e6_out[15], demultiplexer_2_out0[4]);  // OR_Gate
  and and_66 (and_66_out, demultiplexer_2_out0[21], clrregs);
  not not_24 (not_24_out, in_3);
  buf or_54 (or_54_out, demultiplexer_2_out0[17]);  // OR_Gate
  buf or_55 (or_55_out[15], demultiplexer_2_out0[8]);  // OR_Gate
  buf mem_inc_r1_d00384f8 (mem_inc_r1_d00384f8_out[15], demultiplexer_2_out0[6]);  // OR_Gate
  Register #(.width(32)) register_17 (.D(datareg1), .Q(register_17_q), .clk(and_66_out));  // open: en, clr
  Counter #(.max('h3fff), .width(14)) counter_2 (
    .Q(counter_2_q), .clk(glbclk));  // open: load, D, count, carry, up, clr
  assign and_67_out = register_17_q[15:0] & {16{sp_hp_8f3679f7}};  // AND_Gate and_67, 16 bits wide
  // RGB_Video rgb_video_1: pin names not known; wires that end beside it: glbclk, not_24_out, counter_2_q[6:0], counter_2_q[6:0], counter_2_q[13:7], counter_2_q[13:7], ram_2_dout, ram_2_dout
  and and_68 (and_68_out, clrregs, demultiplexer_2_out0[20]);
  not not_25 (not_25_out[15], sp_hp_8f3679f7);
  assign and_69_out = datareg1 & {32{demultiplexer_3_out1[31]}};  // AND_Gate and_69, 32 bits wide
  assign and_70_out = datareg1 & {32{demultiplexer_3_out25[31]}};  // AND_Gate and_70, 32 bits wide
  assign and_71_out = or_31_out & {32{demultiplexer_3_out0[31]}};  // AND_Gate and_71, 32 bits wide
  assign and_72_out = datareg1 & {32{demultiplexer_3_out26[31]}};  // AND_Gate and_72, 32 bits wide
  assign and_73_out = {32{demultiplexer_3_out26[31]}} & or_31_out;  // AND_Gate and_73, 32 bits wide
  assign and_74_out = datareg1 & {32{demultiplexer_3_out27[31]}};  // AND_Gate and_74, 32 bits wide
  assign and_75_out = {32{demultiplexer_3_out27[31]}} & or_31_out;  // AND_Gate and_75, 32 bits wide
  assign and_76_out = datareg1 & {32{demultiplexer_3_out28[31]}};  // AND_Gate and_76, 32 bits wide
  assign and_77_out = {32{demultiplexer_3_out28[31]}} & or_31_out;  // AND_Gate and_77, 32 bits wide
  assign and_78_out = datareg1 & {32{demultiplexer_3_out29[31]}};  // AND_Gate and_78, 32 bits wide
  assign and_79_out = {32{demultiplexer_3_out29[31]}} & or_31_out;  // AND_Gate and_79, 32 bits wide
  assign and_80_out = datareg1 & {32{demultiplexer_3_out30[31]}};  // AND_Gate and_80, 32 bits wide
  assign and_81_out = {32{demultiplexer_3_out30[31]}} & or_31_out;  // AND_Gate and_81, 32 bits wide
  assign and_82_out = datareg1 & {32{demultiplexer_3_out31[31]}};  // AND_Gate and_82, 32 bits wide
  assign and_83_out = {32{demultiplexer_3_out31[31]}} & or_31_out;  // AND_Gate and_83, 32 bits wide
  assign out_42 = adder_7_out | subtractor_8_out | multiplier_1_out | divider_1_out | shifter_2_out | shifter_1_out | negator_1_out | and_71_out | and_69_out | or_71_out;  // OR_Gate or_56, 32 bits wide
  Register #(.width(32)) register_18 (.D(datareg1), .Q(register_18_q), .clk(and_68_out));  // open: en, clr
  Negator #(.width(32)) negator_1 (.in(and_70_out), .out(negator_1_out));
  Divider #(.width(32)) divider_1 (.a(and_76_out), .b(and_77_out), .out(divider_1_out));  // open: upper, rem
  Multiplier #(.width(32)) multiplier_1 (.a(and_78_out), .b(and_79_out), .out(multiplier_1_out));  // open: cin, cout
  Subtractor #(.width(32)) subtractor_8 (.a(and_80_out), .b(and_81_out), .out(subtractor_8_out));  // open: bin, bout
  Adder #(.width(32)) adder_7 (.a(and_82_out), .b(and_83_out), .out(adder_7_out));  // open: cin, cout
  assign and_84_out = {16{not_25_out[15]}} & register_18_q[15:0];  // AND_Gate and_84, 16 bits wide
  assign or_57_out = and_67_out | and_84_out;  // OR_Gate or_57, 16 bits wide
  Shifter #(.shift("lr"), .width(32)) shifter_1 (.in(and_72_out), .\dist (and_73_out[4:0]), .out(shifter_1_out));
  Shifter #(.width(32)) shifter_2 (.in(and_74_out), .\dist (and_75_out[4:0]), .out(shifter_2_out));
  or or_58 (or_58_out, demultiplexer_2_out0[1], demultiplexer_2_out0[10], demultiplexer_2_out0[18]);
  or or_59 (or_59_out, demultiplexer_1_out0[28], demultiplexer_1_out0[29]);
  LED led_1 (.in(clrregs));
  LED led_2 (.in(d_ff_9_q[6]));
  LED led_3 (.in(d_ff_9_q[5]));
  or or_60 (or_60_out, demultiplexer_2_out0[2], demultiplexer_1_out0[30], demultiplexer_2_out0[0], demultiplexer_1_out0[31], or_58_out);
  or enable_print_9bcf9a48 (enable_print_9bcf9a48_out, demultiplexer_1_out0[24], demultiplexer_1_out0[25]);
  and and_85 (and_85_out, demultiplexer_1_out0[22], d_ff_9_q[6]);
  LED led_4 (.in(d_ff_9_q[4]));
  LED led_5 (.in(d_ff_9_q[3]));
  LED led_6 (.in(d_ff_9_q[2]));
  LED led_7 (.in(d_ff_9_q[1]));
  or or_61 (or_61_out, demultiplexer_1_out0[19], demultiplexer_1_out0[20]);
  and and_86 (and_86_out, d_ff_19_q, enable_print_9bcf9a48_out);
  Register #(.width(32)) register_19 (.D(or_29_out), .Q(register_19_q), .clk(and_85_out));  // open: en, clr
  LED led_8 (.in(d_ff_9_q[0]));
  led_matrix_module led_matrix_module_1 (
    .clk(and_86_out), .inp_0_3c70ccdc(or_29_out[0]), .inp1(or_29_out[1]), .inp2(or_29_out[2]),
    .inp3(or_29_out[3]), .inp_4_30ff2636(or_29_out[4]), .inp_5_b9744d22(or_29_out[5]),
    .inp_6_a33c554e(or_29_out[6]), .High_Low_7840782d(or_29_out[7]),
    .out_4_687d40bf(led_matrix_module_1_out_4_687d40bf), .out_0_53574313(led_matrix_module_1_out_0_53574313),
    .out_1_2d638d36(led_matrix_module_1_out_1_2d638d36), .out_3_89d83ed1(led_matrix_module_1_out_3_89d83ed1));
  and and_87 (and_87_out, d_ff_19_q, demultiplexer_1_out0[21]);
  Demultiplexer #(.enable("true"), .select(5)) demultiplexer_3 (
    .out0(demultiplexer_3_out0[31]), .out1(demultiplexer_3_out1[31]), .out3(demultiplexer_3_out3[31]),
    .out4(demultiplexer_3_out4[31]), .out5(demultiplexer_3_out5[31]), .out6(demultiplexer_3_out6[31]),
    .out7(demultiplexer_3_out7[31]), .out8(demultiplexer_3_out8[31]), .out9(demultiplexer_3_out9[31]),
    .out10(demultiplexer_3_out10[31]), .out11(demultiplexer_3_out11[31]), .out25(demultiplexer_3_out25[31]),
    .out26(demultiplexer_3_out26[31]), .out27(demultiplexer_3_out27[31]), .out28(demultiplexer_3_out28[31]),
    .out29(demultiplexer_3_out29[31]), .out30(demultiplexer_3_out30[31]), .out31(demultiplexer_3_out31[31]),
    .in(1'b1), .sel(out_32[4:0]));  // open: out2, out12, out13, out14, out15, out16, out17, out18, out19, out20, out21, out22, out23, out24, en
  or or_62 (or_62_out, not_26_out, d_ff_38_q);
  or or_63 (or_63_out, keyboard_1_avail, d_ff_37_q);
  not not_26 (not_26_out, or_65_out);
  Register #(.width(32)) register_20 (
    .D(or_29_out), .Q({register_20_q_3, register_20_q_2, register_20_q}), .clk(and_88_out));  // open: en, clr
  and and_88 (and_88_out, or_59_out, d_ff_9_q[6]);
  or or_64 (or_64_out, out_32[12], d_ff_37_q);
  and and_89 (and_89_out, or_64_out, or_63_out, glbclk);
  D_Flip_Flop d_ff_35 (.clk(and_89_out), .D(or_62_out), .Q(d_ff_35_q));  // open: Qn, preset, reset
  or or_65 (or_65_out, d_ff_38_q, d_ff_36_q, d_ff_35_q);
  and and_90 (and_90_out, d_ff_35_q, keyboard_1_avail);
  and and_91 (and_91_out, d_ff_37_q, keyboard_1_avail);
  D_Flip_Flop d_ff_36 (.clk(and_89_out), .D(d_ff_35_q), .Q(d_ff_36_q));  // open: Qn, preset, reset
  D_Flip_Flop d_ff_37 (.clk(and_89_out), .D(d_ff_36_q), .Q(d_ff_37_q));  // open: Qn, preset, reset
  D_Flip_Flop d_ff_38 (.D(d_ff_37_q), .Q(d_ff_38_q));  // open: clk, Qn, preset, reset
  Divider #(.width(32)) divider_2 (.a(and_93_out), .b(and_94_out), .out(divider_2_out));  // open: upper, rem
  Multiplier #(.width(32)) multiplier_2 (.a(divider_2_out), .b(and_94_out), .out(multiplier_2_out));  // open: cin, cout
  Subtractor #(.width(32)) subtractor_9 (
    .a(and_93_out), .b(multiplier_2_out), .out(subtractor_9_out));  // open: bin, bout
  or or_66 (or_66_out, not_27_out, d_ff_41_q);
  and and_92 (and_92_out, glbclk, keyboard_2_avail);
  not not_27 (not_27_out, or_67_out);
  Keyboard keyboard_2 (.clk(d_ff_41_q), .avail(keyboard_2_avail), .data(keyboard_2_data));  // open: re, clr
  D_Flip_Flop d_ff_39 (.clk(and_92_out), .D(or_66_out), .Q(d_ff_39_q));  // open: Qn, preset, reset
  or or_67 (or_67_out, d_ff_41_q, d_ff_40_q, d_ff_39_q);
  assign and_93_out = datareg1 & {32{demultiplexer_3_out11[31]}};  // AND_Gate and_93, 32 bits wide
  assign and_94_out = {32{demultiplexer_3_out11[31]}} & or_31_out;  // AND_Gate and_94, 32 bits wide
  assign and_95_out = datareg1 & {32{demultiplexer_3_out10[31]}};  // AND_Gate and_95, 32 bits wide
  assign and_96_out = {32{demultiplexer_3_out10[31]}} & or_31_out;  // AND_Gate and_96, 32 bits wide
  assign and_97_out = datareg1 & {32{demultiplexer_3_out9[31]}};  // AND_Gate and_97, 32 bits wide
  assign and_98_out = {32{demultiplexer_3_out9[31]}} & or_31_out;  // AND_Gate and_98, 32 bits wide
  assign and_99_out = datareg1 & {32{demultiplexer_3_out8[31]}};  // AND_Gate and_99, 32 bits wide
  assign and_100_out = {32{demultiplexer_3_out8[31]}} & or_31_out;  // AND_Gate and_100, 32 bits wide
  assign and_101_out = datareg1 & {32{demultiplexer_3_out7[31]}};  // AND_Gate and_101, 32 bits wide
  assign and_102_out = {32{demultiplexer_3_out7[31]}} & or_31_out;  // AND_Gate and_102, 32 bits wide
  assign and_103_out = datareg1 & {32{demultiplexer_3_out6[31]}};  // AND_Gate and_103, 32 bits wide
  assign and_104_out = {32{demultiplexer_3_out6[31]}} & or_31_out;  // AND_Gate and_104, 32 bits wide
  assign and_105_out = datareg1 & {32{demultiplexer_3_out5[31]}};  // AND_Gate and_105, 32 bits wide
  assign and_106_out = {32{demultiplexer_3_out5[31]}} & or_31_out;  // AND_Gate and_106, 32 bits wide
  assign and_107_out = datareg1 & {32{demultiplexer_3_out4[31]}};  // AND_Gate and_107, 32 bits wide
  assign and_108_out = {32{demultiplexer_3_out4[31]}} & or_31_out;  // AND_Gate and_108, 32 bits wide
  assign and_109_out = datareg1 & {32{demultiplexer_3_out3[31]}};  // AND_Gate and_109, 32 bits wide
  assign and_110_out = {32{demultiplexer_3_out3[31]}} & or_31_out;  // AND_Gate and_110, 32 bits wide
  D_Flip_Flop d_ff_40 (.clk(and_92_out), .D(d_ff_39_q), .Q(d_ff_40_q));  // open: Qn, preset, reset
  Register #(.width(7)) register_21 (
    .D(keyboard_2_data), .Q(out_29[6:0]), .clk(d_ff_39_q), .clr(demultiplexer_1_out0[27]));  // open: en
  or or_68 (or_68_out, comparator_3_eq, comparator_3_lt);
  Comparator #(.width(32)) comparator_3 (
    .a(and_95_out), .b(and_96_out), .eq(comparator_3_eq), .lt(comparator_3_lt));  // open: gt
  and and_111 (and_111_out, demultiplexer_3_out10[31], or_68_out);
  or or_69 (or_69_out, comparator_4_gt, comparator_4_eq);
  Comparator #(.width(32)) comparator_4 (
    .a(and_97_out), .b(and_98_out), .gt(comparator_4_gt), .eq(comparator_4_eq));  // open: lt
  and and_112 (and_112_out, demultiplexer_3_out9[31], or_69_out);
  Comparator #(.width(32)) comparator_5 (.a(and_99_out), .b(and_100_out), .lt(comparator_5_lt));  // open: gt, eq
  and and_113 (and_113_out, demultiplexer_3_out8[31], comparator_5_lt);
  Comparator #(.width(32)) comparator_6 (.a(and_101_out), .b(and_102_out), .gt(comparator_6_gt));  // open: eq, lt
  and and_114 (and_114_out, demultiplexer_3_out7[31], comparator_6_gt);
  not not_28 (not_28_out, comparator_7_eq);
  Comparator #(.width(32)) comparator_7 (.a(and_103_out), .b(and_104_out), .eq(comparator_7_eq));  // open: gt, lt
  and and_115 (and_115_out, demultiplexer_3_out6[31], not_28_out);
  Comparator #(.width(32)) comparator_8 (.a(and_105_out), .b(and_106_out), .eq(comparator_8_eq));  // open: gt, lt
  and and_116 (and_116_out, demultiplexer_3_out5[31], comparator_8_eq);
  assign or_70_out = and_107_out | and_108_out;  // OR_Gate or_70, 32 bits wide
  assign and_117_out = and_109_out & and_110_out;  // AND_Gate and_117, 32 bits wide
  assign or_71_out = and_117_out | or_70_out | subtractor_9_out | {{31{1'b0}}, or_72_out[0]};  // OR_Gate or_71, 32 bits wide
  D_Flip_Flop d_ff_41 (.clk(and_92_out), .D(d_ff_40_q), .Q(d_ff_41_q));  // open: Qn, preset, reset
  Keyboard keyboard_3 (.clk(undriven), .avail(keyboard_3_avail), .data(keyboard_3_data));  // open: re, clr
  LED led_9 (.in(led_matrix_module_1_out_0_53574313[0]));
  or or_72 (or_72_out[0], and_111_out, and_112_out, and_113_out, and_114_out, and_115_out, and_116_out);

  assign out_29[31:7] = {25{1'b0}};
  assign out_30[31:7] = {25{1'b0}};
  assign out_34 = in_5;
  assign out_35 = in_6;
  assign out_36 = in_7;
  assign out_37 = in_8;
  assign out_38 = in_9;
  assign out_39 = in_10;
  assign out_40 = in_11;
  assign out_41 = in_12;

  // Other names for the same wires on the sheet: pc_output[23:0] = ip; rom_address[23:0] = ip; en_write = out_32[17];
  //   pc_load_data[23:0] = out_25; rom_data[31:0] = out_26

  // Notes on the sheet:
  //   contents of rom_1 (hex, n*v repeats v):
  //   8c000000 3fffc03 2c003c00 3c00 80000000 c03 a8000000 5b803 48000c00 0 88001c00 3 94000000 6000
  //   a4001c00 3 d0001c00 3 94000000 1403 2c003000 c01c b4000000 3000001c 2c003000 1f b7fffc00 3000001f
  //   2c003000 281f 2c002000 1f b4002000 c e4002000 3000301f 34003000 13 3c000000 13000 40000000 13000
  //   2c003000 281f 2c002000 1f b40023ff fc00000f c002000 3000301f 88003000 1b 2c003000 1f b4003000 c
  //   84000000 2007 4002000 3000301f 88003000 1b 2c003000 c01f 84000000 2007 8002000 3000301f b7fffc00
  //   3000000f 48000000 4 50000000 1c 68000000 7000 2c003000 1f b40033ff fc00001f 78009000 3000001b
  //   68000000 15003 90001c00 3 9c000000 6003 84000000 1c03 d0001c00 1 c4000000 3 88001c00 3 94000000 6000
  //   a4001c00 3 d0001c00 3 94000000 5003 2c003000 1f b4000000 3000001f 2c003000 41f b7fff000 3000001f
  //   2c003000 281f 2c002000 1f b4002000 f e4002000 3000301f 34003000 13 3c000000 24000 40000000 24000
  //   48000000 7 88000000 1b 2c003000 41f 2c002000 1f b40023ff f000000f 4002000 3000301f b7fff000 3000000f
  //   50000000 1c 68000000 1c000 2c003000 1f b40033ff f000001f 20003000 101f 4003c00 30003c0b b7ffe000
  //   3c000017 2c003000 1f b40033ff f000001f 2c001000 1f b4001000 3000001f 2c003000 1f 200033ff fffff01f
  //   d7ffe000 1f 78003000 1000003f 2c003000 41f b7ffd000 3000001f 2c003000 1f b7ffc000 3000001f 2c003000
  //   1f b40033ff f000000f 2c002000 1f b40023ff d000000f e4002000 3000301f 34003000 13 3c000000 38800
  //   40000000 38800 840003ff ffffc007 2c003000 1f b40033ff c000001f 2c001000 1f b4001000 3000001f
  //   2c003000 1f b40033ff d000001f 200033ff fffff01f d7ffe000 1f 78003000 1000003f 2c003000 41f 2c002000
  //   1f b40023ff d000000f 4002000 3000301f b7ffd000 3000000f 68000000 2c800 2c003000 1f b40033ff e000001f
  //   78009000 3000001b 68000000 3a803 90001c00 3 9c000000 6003 84000000 1c03 d0001c00 1 c4000000 3
  //   88001c00 3 94000000 6000 a4001c00 3 d0001c00 3 94000000 2003 2c003000 41f 88003000 1b 2c003000 1f
  //   200033ff fffff01f 2c001000 1f b4001000 3000001f d400a000 1f b8001000 105f 2c002000 1f b4002000
  //   1000001f 84000000 3007 8002000 3000301f b4000000 3000001f 2c003000 41f 2c002000 1f b4002000 f
  //   e4002000 3000301f 34003000 13 3c000000 52000 40000000 52000 2c003000 1f b4003000 1f 200033ff
  //   fffff01f 2c001000 1f b4001000 3000001f d400a000 1f b8001000 105f 2c003000 1f b4003000 1000001f
  //   b7fff000 3000001f 53fff000 1c 2c003000 41f 2c002000 1f b4002000 f 8002000 3000301f b4000000 3000000f
  //   68000000 46000 90001c00 3 9c000000 6003 84000000 1c03 d0001c00 1 c4000000 3 88001c00 3 94000000 6000
  //   a4001c00 3 d0001c00 3 94000000 1003 2c003000 1f b4003000 a000001f b4000000 3000001f 50000000 1c
  //   90001c00 3 9c000000 6003 84000000 1c03 d0001c00 1 c4000000 3 88001c00 3 94000000 6000 a4001c00 3
  //   d0001c00 3 94000000 3 4c000000 f400 4c000000 f400 4c000000 f400 4c000000 8000 4c000000 13000
  //   4c000000 1a400 4c000000 19c00 4c000000 1a000 4c000000 1d000 4c000000 1dc00 4c000000 19400 4c000000
  //   1a400 4c000000 19c00 4c000000 1a000 4c000000 1d000 4c000000 8000 4c000000 12400 4c000000 1b800
  //   4c000000 1cc00 4c000000 1d000 4c000000 1c800 4c000000 1d400 4c000000 18c00 4c000000 1d000 4c000000
  //   1a400 4c000000 1bc00 4c000000 1b800 4c000000 8000 4c000000 14c00 4c000000 19400 4c000000 1d000
  //   4c000000 8000 4c000000 10400 4c000000 1c800 4c000000 1d000 4c000000 1a400 4c000000 1d000 4c000000
  //   19400 4c000000 18c00 4c000000 1a000 4c000000 1d000 4c000000 1d400 4c000000 1c800 4c000000 19400
  //   4c000000 8000 4c000000 14000 4c000000 14800 4c000000 13c00 4c000000 10c00 4c000000 11400 4c000000
  //   14c00 4c000000 14c00 4c000000 13c00 4c000000 14800 4c000000 8000 4c000000 11000 4c000000 11400
  //   4c000000 13400 4c000000 13c00 4c000000 8000 4c000000 f400 4c000000 f400 4c000000 f400 4c000000 2800
  //   4c000000 13000 4c000000 12400 4c000000 14c00 4c000000 10400 4c000000 8000 4c000000 1a400 4c000000
  //   1cc00 4c000000 8000 4c000000 18400 4c000000 8000 4c000000 18c00 4c000000 1d400 4c000000 1cc00
  //   4c000000 1d000 4c000000 1bc00 4c000000 1b400 4c000000 8000 4c000000 1b400 4c000000 1d400 4c000000
  //   1b000 4c000000 1d000 4c000000 1a400 4c000000 b400 4c000000 18c00 4c000000 1e400 4c000000 18c00
  //   4c000000 1b000 4c000000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
  //   parsed size
  //   direct wr
  //   dir stack inc
  //   mem stack inc
  //   dir stack dec
  //   mem stack dec
  //   cls
  //   set copy add
  //   mov to add
  //   digital write
  //   clr el
  //   write int
  //   CLK
  //   AVALIABLE
  //   KEYBOARD CLK
  //   data
  //   CLK
  //   KEYBOARD CLK
  //   data
endmodule

module ic7476_kj_61a32d8c (
  input  in_1,
  input  in_2,
  output out_3
);

  // D_Flip_Flop d_ff_1: pin names not known; wires that end beside it: in_1, in_2, out_3
endmodule

module ic_74LS74_56b71336 (
  input  clr1,
  input  vcc,
  input  d1,
  input  L_2cls_1264bc87,
  input  L_1clk_057a5169,
  input  L_2d_fb6c4deb,
  input  prs,
  input  L_2clk_df490cc5,
  input  L_2pr_e8437cbd,
  input  gnd,
  output q1,
  output q1_99c70932,
  output q,
  output q_e5aa6a17
);

  D_Flip_Flop d_ff_1 (.clk(L_1clk_057a5169), .D(d1), .Q(q1), .Qn(q1_99c70932), .preset(prs), .reset(clr1));
  D_Flip_Flop d_ff_2 (
    .clk(L_2clk_df490cc5), .D(L_2d_fb6c4deb), .Q(q), .Qn(L_2d_fb6c4deb), .preset(L_2pr_e8437cbd),
    .reset(L_2cls_1264bc87));

  assign q_e5aa6a17 = L_2d_fb6c4deb;
endmodule

module led_matrix_module (
  input  clk,
  input  inp_0_3c70ccdc,
  input  inp1,
  input  inp2,
  input  inp3,
  input  inp_4_30ff2636,
  input  inp_5_b9744d22,
  input  inp_6_a33c554e,
  input  High_Low_7840782d,
  output [31:0] out_4_687d40bf,
  output [31:0] out_0_53574313,
  output [31:0] out_1_2d638d36,
  output [31:0] out_3_89d83ed1
);

  wire and_1_out, and_2_out, and_3_out, and_4_out, not_1_out, not_3_out;
  wire [31:0] and_5_out, and_6_out, and_7_out, and_8_out, and_9_out, and_10_out, and_11_out, and_12_out,
       and_13_out, and_14_out, and_15_out, and_16_out, and_17_out, and_18_out, and_19_out, and_20_out,
       demultiplexer_1_out0, demultiplexer_2_out0, demultiplexer_3_out0, demultiplexer_4_out0, not_2_out,
       not_4_out, not_5_out, not_6_out, not_7_out, not_8_out, not_9_out, not_10_out, not_11_out, not_12_out,
       or_1_out, or_2_out, or_3_out, register_4_p3, register_4_p5, register_4_p6;

  not not_1 (not_1_out, inp_6_a33c554e);
  assign not_2_out = ~{32{High_Low_7840782d}};  // NOT_Gate not_2, 32 bits wide
  not not_3 (not_3_out, inp_5_b9744d22);
  assign not_4_out = ~demultiplexer_1_out0;  // NOT_Gate not_4, 32 bits wide
  Demultiplexer #(.enable("true"), .select(5)) demultiplexer_1 (
    .out0(demultiplexer_1_out0[0]), .out1(demultiplexer_1_out0[1]), .out2(demultiplexer_1_out0[2]),
    .out3(demultiplexer_1_out0[3]), .out4(demultiplexer_1_out0[4]), .out5(demultiplexer_1_out0[5]),
    .out6(demultiplexer_1_out0[6]), .out7(demultiplexer_1_out0[7]), .out8(demultiplexer_1_out0[8]),
    .out9(demultiplexer_1_out0[9]), .out10(demultiplexer_1_out0[10]), .out11(demultiplexer_1_out0[11]),
    .out12(demultiplexer_1_out0[12]), .out13(demultiplexer_1_out0[13]), .out14(demultiplexer_1_out0[14]),
    .out15(demultiplexer_1_out0[15]), .out16(demultiplexer_1_out0[16]), .out17(demultiplexer_1_out0[17]),
    .out18(demultiplexer_1_out0[18]), .out19(demultiplexer_1_out0[19]), .out20(demultiplexer_1_out0[20]),
    .out21(demultiplexer_1_out0[21]), .out22(demultiplexer_1_out0[22]), .out23(demultiplexer_1_out0[23]),
    .out24(demultiplexer_1_out0[24]), .out25(demultiplexer_1_out0[25]), .out26(demultiplexer_1_out0[26]),
    .out27(demultiplexer_1_out0[27]), .out28(demultiplexer_1_out0[28]), .out29(demultiplexer_1_out0[29]),
    .out30(demultiplexer_1_out0[30]), .out31(demultiplexer_1_out0[31]), .in(and_1_out),
    .sel({inp_4_30ff2636, inp3, inp2, inp1, inp_0_3c70ccdc}));  // open: en
  and and_1 (and_1_out, not_3_out, not_1_out);
  and and_2 (and_2_out, inp_5_b9744d22, not_1_out);
  and and_3 (and_3_out, not_3_out, inp_6_a33c554e);
  and and_4 (and_4_out, inp_5_b9744d22, inp_6_a33c554e);
  Register #(.width(32)) register_1 (.D(or_1_out), .Q(out_0_53574313), .clk(clk));  // open: en, clr
  assign not_5_out = ~out_0_53574313;  // NOT_Gate not_5, 32 bits wide
  assign and_5_out = not_2_out & not_4_out & out_0_53574313;  // AND_Gate and_5, 32 bits wide
  assign and_6_out = {32{High_Low_7840782d}} & not_4_out & out_0_53574313;  // AND_Gate and_6, 32 bits wide
  assign or_1_out = and_5_out | and_6_out | and_7_out | and_8_out;  // OR_Gate or_1, 32 bits wide
  assign and_7_out = {32{High_Low_7840782d}} & demultiplexer_1_out0 & not_5_out;  // AND_Gate and_7, 32 bits wide
  assign and_8_out = {32{High_Low_7840782d}} & demultiplexer_1_out0 & out_0_53574313;  // AND_Gate and_8, 32 bits wide
  assign not_6_out = ~demultiplexer_2_out0;  // NOT_Gate not_6, 32 bits wide
  assign not_7_out = ~{32{High_Low_7840782d}};  // NOT_Gate not_7, 32 bits wide
  Demultiplexer #(.enable("true"), .select(5)) demultiplexer_2 (
    .out0(demultiplexer_2_out0[0]), .out1(demultiplexer_2_out0[1]), .out2(demultiplexer_2_out0[2]),
    .out3(demultiplexer_2_out0[3]), .out4(demultiplexer_2_out0[4]), .out5(demultiplexer_2_out0[5]),
    .out6(demultiplexer_2_out0[6]), .out7(demultiplexer_2_out0[7]), .out8(demultiplexer_2_out0[8]),
    .out9(demultiplexer_2_out0[9]), .out10(demultiplexer_2_out0[10]), .out11(demultiplexer_2_out0[11]),
    .out12(demultiplexer_2_out0[12]), .out13(demultiplexer_2_out0[13]), .out14(demultiplexer_2_out0[14]),
    .out15(demultiplexer_2_out0[15]), .out16(demultiplexer_2_out0[16]), .out17(demultiplexer_2_out0[17]),
    .out18(demultiplexer_2_out0[18]), .out19(demultiplexer_2_out0[19]), .out20(demultiplexer_2_out0[20]),
    .out21(demultiplexer_2_out0[21]), .out22(demultiplexer_2_out0[22]), .out23(demultiplexer_2_out0[23]),
    .out24(demultiplexer_2_out0[24]), .out25(demultiplexer_2_out0[25]), .out26(demultiplexer_2_out0[26]),
    .out27(demultiplexer_2_out0[27]), .out28(demultiplexer_2_out0[28]), .out29(demultiplexer_2_out0[29]),
    .out30(demultiplexer_2_out0[30]), .out31(demultiplexer_2_out0[31]), .in(and_2_out),
    .sel({inp_4_30ff2636, inp3, inp2, inp1, inp_0_3c70ccdc}));  // open: en
  Register #(.width(32)) register_2 (.D(or_2_out), .Q(out_1_2d638d36), .clk(clk));  // open: en, clr
  assign not_8_out = ~out_1_2d638d36;  // NOT_Gate not_8, 32 bits wide
  assign and_9_out = not_7_out & not_6_out & out_1_2d638d36;  // AND_Gate and_9, 32 bits wide
  assign and_10_out = {32{High_Low_7840782d}} & not_6_out & out_1_2d638d36;  // AND_Gate and_10, 32 bits wide
  assign and_11_out = {32{High_Low_7840782d}} & demultiplexer_2_out0 & not_8_out;  // AND_Gate and_11, 32 bits wide
  assign and_12_out = {32{High_Low_7840782d}} & demultiplexer_2_out0 & out_1_2d638d36;  // AND_Gate and_12, 32 bits wide
  assign or_2_out = and_9_out | and_10_out | and_11_out | and_12_out;  // OR_Gate or_2, 32 bits wide
  assign not_9_out = ~{32{High_Low_7840782d}};  // NOT_Gate not_9, 32 bits wide
  Register #(.width(32)) register_3 (.D(or_3_out), .Q(out_3_89d83ed1), .clk(clk));  // open: en, clr
  assign not_10_out = ~demultiplexer_3_out0;  // NOT_Gate not_10, 32 bits wide
  assign not_11_out = ~out_3_89d83ed1;  // NOT_Gate not_11, 32 bits wide
  Demultiplexer #(.enable("true"), .select(5)) demultiplexer_3 (
    .out0(demultiplexer_3_out0[0]), .out1(demultiplexer_3_out0[1]), .out2(demultiplexer_3_out0[2]),
    .out3(demultiplexer_3_out0[3]), .out4(demultiplexer_3_out0[4]), .out5(demultiplexer_3_out0[5]),
    .out6(demultiplexer_3_out0[6]), .out7(demultiplexer_3_out0[7]), .out8(demultiplexer_3_out0[8]),
    .out9(demultiplexer_3_out0[9]), .out10(demultiplexer_3_out0[10]), .out11(demultiplexer_3_out0[11]),
    .out12(demultiplexer_3_out0[12]), .out13(demultiplexer_3_out0[13]), .out14(demultiplexer_3_out0[14]),
    .out15(demultiplexer_3_out0[15]), .out16(demultiplexer_3_out0[16]), .out17(demultiplexer_3_out0[17]),
    .out18(demultiplexer_3_out0[18]), .out19(demultiplexer_3_out0[19]), .out20(demultiplexer_3_out0[20]),
    .out21(demultiplexer_3_out0[21]), .out22(demultiplexer_3_out0[22]), .out23(demultiplexer_3_out0[23]),
    .out24(demultiplexer_3_out0[24]), .out25(demultiplexer_3_out0[25]), .out26(demultiplexer_3_out0[26]),
    .out27(demultiplexer_3_out0[27]), .out28(demultiplexer_3_out0[28]), .out29(demultiplexer_3_out0[29]),
    .out30(demultiplexer_3_out0[30]), .out31(demultiplexer_3_out0[31]), .in(and_3_out),
    .sel({inp_4_30ff2636, inp3, inp2, inp1, inp_0_3c70ccdc}));  // open: en
  assign and_13_out = not_9_out & not_10_out & out_3_89d83ed1;  // AND_Gate and_13, 32 bits wide
  assign and_14_out = {32{High_Low_7840782d}} & not_10_out & out_3_89d83ed1;  // AND_Gate and_14, 32 bits wide
  assign and_15_out = {32{High_Low_7840782d}} & demultiplexer_3_out0 & not_11_out;  // AND_Gate and_15, 32 bits wide
  assign and_16_out = {32{High_Low_7840782d}} & demultiplexer_3_out0 & out_3_89d83ed1;  // AND_Gate and_16, 32 bits wide
  assign or_3_out = and_13_out | and_14_out | and_15_out | and_16_out;  // OR_Gate or_3, 32 bits wide
  assign not_12_out = ~{32{High_Low_7840782d}};  // NOT_Gate not_12, 32 bits wide
  // Register #(.width(32)) register_4: pin names not known; wires that end beside it: clk, out_4_687d40bf, register_4_p3, out_4_687d40bf, register_4_p5, register_4_p6, register_4_p3
  assign register_4_p5 = ~demultiplexer_4_out0;  // NOT_Gate not_13, 32 bits wide
  Demultiplexer #(.enable("true"), .select(5)) demultiplexer_4 (
    .out0(demultiplexer_4_out0[0]), .out1(demultiplexer_4_out0[1]), .out2(demultiplexer_4_out0[2]),
    .out3(demultiplexer_4_out0[3]), .out4(demultiplexer_4_out0[4]), .out5(demultiplexer_4_out0[5]),
    .out6(demultiplexer_4_out0[6]), .out7(demultiplexer_4_out0[7]), .out8(demultiplexer_4_out0[8]),
    .out9(demultiplexer_4_out0[9]), .out10(demultiplexer_4_out0[10]), .out11(demultiplexer_4_out0[11]),
    .out12(demultiplexer_4_out0[12]), .out13(demultiplexer_4_out0[13]), .out14(demultiplexer_4_out0[14]),
    .out15(demultiplexer_4_out0[15]), .out16(demultiplexer_4_out0[16]), .out17(demultiplexer_4_out0[17]),
    .out18(demultiplexer_4_out0[18]), .out19(demultiplexer_4_out0[19]), .out20(demultiplexer_4_out0[20]),
    .out21(demultiplexer_4_out0[21]), .out22(demultiplexer_4_out0[22]), .out23(demultiplexer_4_out0[23]),
    .out24(demultiplexer_4_out0[24]), .out25(demultiplexer_4_out0[25]), .out26(demultiplexer_4_out0[26]),
    .out27(demultiplexer_4_out0[27]), .out28(demultiplexer_4_out0[28]), .out29(demultiplexer_4_out0[29]),
    .out30(demultiplexer_4_out0[30]), .out31(demultiplexer_4_out0[31]), .in(and_4_out),
    .sel({inp_4_30ff2636, inp3, inp2, inp1, inp_0_3c70ccdc}));  // open: en
  assign register_4_p6 = ~out_4_687d40bf;  // NOT_Gate not_14, 32 bits wide
  assign and_17_out = not_12_out & register_4_p5 & out_4_687d40bf;  // AND_Gate and_17, 32 bits wide
  assign and_18_out = {32{High_Low_7840782d}} & register_4_p5 & out_4_687d40bf;  // AND_Gate and_18, 32 bits wide
  assign and_19_out = {32{High_Low_7840782d}} & demultiplexer_4_out0 & register_4_p6;  // AND_Gate and_19, 32 bits wide
  assign and_20_out = {32{High_Low_7840782d}} & demultiplexer_4_out0 & out_4_687d40bf;  // AND_Gate and_20, 32 bits wide
  assign register_4_p3 = and_17_out | and_18_out | and_19_out | and_20_out;  // OR_Gate or_4, 32 bits wide
endmodule

module bcd_to_binary (
  input  in_1,
  input  in_2,
  input  [8:0] in_3,
  input  in_4,
  input  in_5,
  input  [8:0] in_6,
  output [15:0] out_7,
  output [15:0] out_8
);

  wire and_1_out, and_2_out, and_3_out, clock_1_out, clock_2_out, d_ff_1_qn, d_ff_2_qn, d_ff_3_q, d_ff_7_p2,
       keyboard_1_avail, keyboard_2_avail, not_1_out, or_1_out, register_1_p4, register_1_p5, register_6_p2,
       register_6_p6, undriven, undriven_2;
  wire [6:0] keyboard_1_data, keyboard_2_data, subtractor_1_out, subtractor_2_out;
  wire [15:0] adder_1_out, adder_2_out, adder_3_out, adder_4_out, adder_5_out, adder_6_out, multiplier_1_out,
       multiplier_2_out, multiplier_3_out, multiplier_4_out, multiplier_5_out, multiplier_6_out,
       multiplier_7_out, multiplier_8_out, register_2_p6, register_3_p3, register_7_p5, register_8_p3,
       undriven_3, undriven_4, undriven_5, undriven_6, undriven_7, undriven_8, undriven_9, undriven_10,
       undriven_11, undriven_12;

  Clock clock_1 (.out(clock_1_out));
  and and_1 (and_1_out, in_5, keyboard_1_avail, clock_1_out);
  Keyboard keyboard_1 (.clk(and_1_out), .avail(keyboard_1_avail), .data(keyboard_1_data));  // open: re, clr
  Clock clock_2 (.out(clock_2_out));
  D_Flip_Flop d_ff_1 (.clk(and_1_out), .D(in_4), .Qn(d_ff_1_qn));  // open: Q, preset, reset
  and and_2 (and_2_out, in_2, keyboard_2_avail, clock_2_out);
  Keyboard keyboard_2 (.clk(and_2_out), .avail(keyboard_2_avail), .data(keyboard_2_data));  // open: re, clr
  Subtractor #(.width(7)) subtractor_1 (
    .a(keyboard_1_data), .b(7'b0110000), .out(subtractor_1_out));  // open: bin, bout
  D_Flip_Flop d_ff_2 (.clk(and_2_out), .D(in_1), .Qn(d_ff_2_qn));  // open: Q, preset, reset
  Subtractor #(.width(7)) subtractor_2 (
    .a(keyboard_2_data), .b(7'b0110000), .out(subtractor_2_out));  // open: bin, bout
  // Register #(.width(16)) register_1: pin names not known; wires that end beside it: {in_6, subtractor_1_out}, and_1_out, and_1_out, register_1_p4, register_1_p5
  // Register #(.width(16)) register_2: pin names not known; wires that end beside it: register_1_p4, register_1_p5, and_1_out, and_1_out, register_1_p5, register_2_p6
  // Register #(.width(16)) register_3: pin names not known; wires that end beside it: register_1_p5, and_1_out, register_3_p3
  Register #(.width(16)) register_4 (.D(register_2_p6), .Q(register_3_p3), .clk(and_1_out));  // open: en, clr
  Register #(.width(16)) register_5 (.D(register_3_p3), .clk(and_1_out));  // open: en, Q, clr
  and and_3 (and_3_out, d_ff_2_qn, not_1_out);
  not not_1 (not_1_out, or_1_out);
  or or_1 (or_1_out, undriven, d_ff_7_p2);
  D_Flip_Flop d_ff_3 (.Q(d_ff_3_q), .Qn(d_ff_3_q));  // open: D, clk, preset, reset
  D_Flip_Flop d_ff_4 (.Q(d_ff_3_q), .Qn(d_ff_3_q));  // open: D, clk, preset, reset
  D_Flip_Flop d_ff_5 (.clk(undriven_2), .Q(d_ff_3_q), .Qn(d_ff_3_q));  // open: D, preset, reset
  D_Flip_Flop d_ff_6 (.Q(d_ff_3_q), .Qn(d_ff_3_q));  // open: D, clk, preset, reset
  // D_Flip_Flop d_ff_7: pin names not known; wires that end beside it: and_2_out, d_ff_7_p2, d_ff_3_q
  // Register #(.width(16)) register_6: pin names not known; wires that end beside it: {in_3, subtractor_2_out}, register_6_p2, and_2_out, and_2_out, register_6_p2, register_6_p6
  // Register #(.width(16)) register_7: pin names not known; wires that end beside it: register_6_p2, register_6_p6, and_2_out, and_2_out, register_7_p5
  // Register #(.width(16)) register_8: pin names not known; wires that end beside it: register_6_p6, and_2_out, register_8_p3
  Register #(.width(16)) register_9 (.D(register_7_p5), .Q(register_8_p3), .clk(and_2_out));  // open: en, clr
  Register #(.width(16)) register_10 (.D(register_8_p3), .clk(and_2_out));  // open: en, Q, clr
  Multiplier #(.width(16)) multiplier_1 (.a(undriven_4), .b(16'ha), .out(multiplier_1_out));  // open: cin, cout
  Adder #(.width(16)) adder_1 (.a(multiplier_1_out), .b(undriven_9), .out(adder_1_out));  // open: cin, cout
  Multiplier #(.width(16)) multiplier_2 (.a(undriven_5), .b(16'ha), .out(multiplier_2_out));  // open: cin, cout
  Multiplier #(.width(16)) multiplier_3 (.a(adder_1_out), .b(16'ha), .out(multiplier_3_out));  // open: cin, cout
  Adder #(.width(16)) adder_2 (.a(multiplier_2_out), .b(undriven_10), .out(adder_2_out));  // open: cin, cout
  Adder #(.width(16)) adder_3 (.a(multiplier_3_out), .b(undriven_11), .out(adder_3_out));  // open: cin, cout
  Multiplier #(.width(16)) multiplier_4 (.a(adder_2_out), .b(16'ha), .out(multiplier_4_out));  // open: cin, cout
  Adder #(.width(16)) adder_4 (.a(multiplier_4_out), .b(undriven_12), .out(adder_4_out));  // open: cin, cout
  Multiplier #(.width(16)) multiplier_5 (.a(adder_3_out), .b(16'ha), .out(multiplier_5_out));  // open: cin, cout
  Multiplier #(.width(16)) multiplier_6 (.a(adder_4_out), .b(16'ha), .out(multiplier_6_out));  // open: cin, cout
  Adder #(.width(16)) adder_5 (.a(multiplier_5_out), .b(undriven_8), .out(adder_5_out));  // open: cin, cout
  Adder #(.width(16)) adder_6 (.a(multiplier_6_out), .b(undriven_3), .out(adder_6_out));  // open: cin, cout
  Multiplier #(.width(16)) multiplier_7 (.a(adder_5_out), .b(16'ha), .out(multiplier_7_out));  // open: cin, cout
  Multiplier #(.width(16)) multiplier_8 (.a(adder_6_out), .b(16'ha), .out(multiplier_8_out));  // open: cin, cout
  Adder #(.width(16)) adder_7 (.a(multiplier_7_out), .b(undriven_6), .out(out_7));  // open: cin, cout
  Adder #(.width(16)) adder_8 (.a(multiplier_8_out), .b(undriven_7), .out(out_8));  // open: cin, cout
endmodule
